// Logisim project riskv.circ as structural Verilog: 16 circuits, main circuit main
module main (
  output [31:0] out_1,
  output [15:0] out_2,
  output [31:0] out_3
);

  wire Asel_t, BrEq_t, BrLt_t, BrUn_t, Bsel, clck, PCsel_t, re_imem_t, Re_t, regwe, we_imem_t, We_t;
  wire [1:0] Ssel_t, WBSel;
  wire [2:0] immgensel, Lsel_t;
  wire [3:0] alusel;
  wire [4:0] insmem_1_rdi, insmem_1_rs1i, insmem_1_rsi2;
  wire [15:0] bitselector_1_out, multiplexer_1_out, pc_1_outpc, shifter_1_out;
  wire [31:0] A_t, dataA, dataB, imm, load, load_to_store, multiplexer_2_out, multiplexer_3_out,
       multiplexer_4_out, Store;

  Multiplexer #(.width(16)) multiplexer_1 (
    .in0(out_2), .in1(bitselector_1_out), .out(multiplexer_1_out), .sel(PCsel_t));
  Clock clock_1 (.out(clck));
  pc pc_1 (.inpc(multiplexer_1_out), .clck(clck), .outpcplus4(out_2), .outpc(pc_1_outpc));
  assign out_1 = {{16{1'b0}}, pc_1_outpc};  // Bit_Extender bit_extender_1
  insmem insmem_1 (
    .address(pc_1_outpc), .we_imem(we_imem_t), .re_imem(re_imem_t), .rdi(insmem_1_rdi), .rs1i(insmem_1_rs1i),
    .rsi2(insmem_1_rsi2), .ins(out_3));
  Multiplexer #(.select(2), .width(32)) multiplexer_2 (
    .in0(load), .in1(A_t), .in2({{16{1'b0}}, out_2}), .out(multiplexer_2_out), .sel(WBSel));  // open: in3
  Immediate_Generator immediate_generator_1 (.ins(out_3), .immsel(immgensel), .imm31_0(imm));
  Control_logic control_logic_1 (
    .istruction(out_3), .BrLt(BrLt_t), .BrEq(BrEq_t), .ALUsle(alusel), .regwe(regwe), .immse(immgensel),
    .Bsel(Bsel), .Lsel(Lsel_t), .Re(Re_t), .we(We_t), .Asel(Asel_t), .WBSel(WBSel), .Ssel(Ssel_t),
    .brUn(BrUn_t), .PCsel(PCsel_t), .re_imm(re_imem_t), .we_imm(we_imem_t));
  Register_File register_file_1 (
    .rd(multiplexer_2_out), .rdi(insmem_1_rdi), .rsi1(insmem_1_rs1i), .rsi2(insmem_1_rsi2), .we(regwe),
    .clck(clck), .rs1(dataA), .rs2(dataB));
  Multiplexer #(.width(32)) multiplexer_3 (.in0(dataA), .in1(out_1), .out(multiplexer_3_out), .sel(Asel_t));
  Multiplexer #(.width(32)) multiplexer_4 (.in0(dataB), .in1(imm), .out(multiplexer_4_out), .sel(Bsel));
  branch_com branch_com_1 (.dataA(dataA), .dataB(dataB), .brUn(BrUn_t), .brLt(BrLt_t), .brEq(BrEq_t));
  BitSelector #(.group(16), .width(32)) bitselector_1 (.in(A_t), .out(bitselector_1_out), .sel(1'b0));
  ALU alu_1 (.dataA(multiplexer_3_out), .dataB(multiplexer_4_out), .sel(alusel), .dataD(A_t));
  Storecircuit storecircuit_1 (.Data(dataB), .Ssel(Ssel_t), .address(A_t), .load(load_to_store), .Store(Store));
  Shifter #(.shift("lr"), .width(16)) shifter_1 (.in(bitselector_1_out), .\dist (4'b0010), .out(shifter_1_out));
  RAM #(.addrWidth(16), .dataWidth(32)) ram_1 (
    .addr(shifter_1_out), .we(We_t), .oe(Re_t), .clk(clck), .din(Store), .dout(load_to_store));
  Loadcircuit loadcircuit_1 (.Adress(A_t), .D(load_to_store), .lSel(Lsel_t), .Loaded(load));

  // Other names for the same wires on the sheet: ins[31:0] = out_3; Pc_t[31:0] = out_1; Pcplus4[15:0] = out_2

  // Notes on the sheet:
  //   i fixed the load circuit
  //   if the wiring closest to the ram is red .remove the ram then undo it .it should return to normal
endmodule

module pc (
  input  [15:0] inpc,
  input  clck,
  output [15:0] outpcplus4,
  output [15:0] outpc
);

  Register #(.width(16)) register_1 (.D(inpc), .en(1'b1), .clk(clck), .Q(outpc));  // open: clr
  Adder #(.width(16)) adder_1 (.a(outpc), .b(16'h1), .out(outpcplus4));  // open: cin, cout

  // Other names for the same wires on the sheet: clck_t = clck; inpc_t[15:0] = inpc; outpc_t[15:0] = outpc;
  //   outpcplus4_t[15:0] = outpcplus4
endmodule

module Register_File (
  input  [31:0] rd,
  input  [4:0] rdi,
  input  [4:0] rsi1,
  input  [4:0] rsi2,
  input  we,
  input  clck,
  output [31:0] rs1,
  output [31:0] rs2
);

  wire x0we_t, x1we_t, x2we_t, x3we_t, x4we_t, x5we_t, x6we_t, x7we_t, x8we_t, x9we_t, x10we_t, x11we_t,
       x12we_t, x13we_t, x14we_t, x15we_t, x16we_t, x17we_t, x18we_t, x19we_t, x20we_t, x21we_t, x22we_t,
       x23we_t, x24we_t, x25we_t, x26we_t, x27we_t, x28we_t, x29we_t, x30we_t, x31we_t;
  wire [31:0] x1_t, x2_t, x3_t, x4_t, x5_t, x6_t, x7_t, x8_t, x9_t, x10_t, x11_t, x12_t, x13_t, x14_t, x15_t,
       x16_t, x17_t, x18_t, x19_t, x20_t, x21_t, x22_t, x23_t, x24_t, x25_t, x26_t, x27_t, x28_t, x29_t,
       x30_t, x31_t;

  Demultiplexer #(.select(5)) demultiplexer_1 (
    .out0(x0we_t), .out1(x1we_t), .out2(x2we_t), .out3(x3we_t), .out4(x4we_t), .out5(x5we_t), .out6(x6we_t),
    .out7(x7we_t), .out8(x8we_t), .out9(x9we_t), .out10(x10we_t), .out11(x11we_t), .out12(x12we_t),
    .out13(x13we_t), .out14(x14we_t), .out15(x15we_t), .out16(x16we_t), .out17(x17we_t), .out18(x18we_t),
    .out19(x19we_t), .out20(x20we_t), .out21(x21we_t), .out22(x22we_t), .out23(x23we_t), .out24(x24we_t),
    .out25(x25we_t), .out26(x26we_t), .out27(x27we_t), .out28(x28we_t), .out29(x29we_t), .out30(x30we_t),
    .out31(x31we_t), .in(we), .sel(rdi));
  Register #(.width(32)) x4 (.D(rd), .en(x4we_t), .clk(clck), .Q(x4_t));  // open: clr
  Register #(.width(32)) x8 (.D(rd), .en(x8we_t), .clk(clck), .Q(x8_t));  // open: clr
  Register #(.width(32)) x12 (.D(rd), .en(x12we_t), .clk(clck), .Q(x12_t));  // open: clr
  Register #(.width(32)) x16 (.D(rd), .en(x16we_t), .clk(clck), .Q(x16_t));  // open: clr
  Register #(.width(32)) x20 (.D(rd), .en(x20we_t), .clk(clck), .Q(x20_t));  // open: clr
  Register #(.width(32)) x24 (.D(rd), .en(x24we_t), .clk(clck), .Q(x24_t));  // open: clr
  Register #(.width(32)) x28 (.D(rd), .en(x28we_t), .clk(clck), .Q(x28_t));  // open: clr
  Register #(.width(32)) x1 (.D(rd), .en(x1we_t), .clk(clck), .Q(x1_t));  // open: clr
  Register #(.width(32)) x5 (.D(rd), .en(x5we_t), .clk(clck), .Q(x5_t));  // open: clr
  Register #(.width(32)) x9 (.D(rd), .en(x9we_t), .clk(clck), .Q(x9_t));  // open: clr
  Register #(.width(32)) x13 (.D(rd), .en(x13we_t), .clk(clck), .Q(x13_t));  // open: clr
  Register #(.width(32)) x17 (.D(rd), .en(x17we_t), .clk(clck), .Q(x17_t));  // open: clr
  Register #(.width(32)) x21 (.D(rd), .en(x21we_t), .clk(clck), .Q(x21_t));  // open: clr
  Register #(.width(32)) x25 (.D(rd), .en(x25we_t), .clk(clck), .Q(x25_t));  // open: clr
  Register #(.width(32)) x29 (.D(rd), .en(x29we_t), .clk(clck), .Q(x29_t));  // open: clr
  Register #(.width(32)) x2 (.D(rd), .en(x2we_t), .clk(clck), .Q(x2_t));  // open: clr
  Register #(.width(32)) x6 (.D(rd), .en(x6we_t), .clk(clck), .Q(x6_t));  // open: clr
  Register #(.width(32)) x10 (.D(rd), .en(x10we_t), .clk(clck), .Q(x10_t));  // open: clr
  Register #(.width(32)) x14 (.D(rd), .en(x14we_t), .clk(clck), .Q(x14_t));  // open: clr
  Register #(.width(32)) x18 (.D(rd), .en(x18we_t), .clk(clck), .Q(x18_t));  // open: clr
  Register #(.width(32)) x22 (.D(rd), .en(x22we_t), .clk(clck), .Q(x22_t));  // open: clr
  Register #(.width(32)) x26 (.D(rd), .en(x26we_t), .clk(clck), .Q(x26_t));  // open: clr
  Register #(.width(32)) x30 (.D(rd), .en(x30we_t), .clk(clck), .Q(x30_t));  // open: clr
  Register #(.width(32)) x3 (.D(rd), .en(x3we_t), .clk(clck), .Q(x3_t));  // open: clr
  Register #(.width(32)) x7 (.D(rd), .en(x7we_t), .clk(clck), .Q(x7_t));  // open: clr
  Register #(.width(32)) x11 (.D(rd), .en(x11we_t), .clk(clck), .Q(x11_t));  // open: clr
  Register #(.width(32)) x15 (.D(rd), .en(x15we_t), .clk(clck), .Q(x15_t));  // open: clr
  Register #(.width(32)) x19 (.D(rd), .en(x19we_t), .clk(clck), .Q(x19_t));  // open: clr
  Register #(.width(32)) x23 (.D(rd), .en(x23we_t), .clk(clck), .Q(x23_t));  // open: clr
  Register #(.width(32)) x27 (.D(rd), .en(x27we_t), .clk(clck), .Q(x27_t));  // open: clr
  Register #(.width(32)) x31 (.D(rd), .en(x31we_t), .clk(clck), .Q(x31_t));  // open: clr
  Multiplexer #(.select(5), .width(32)) multiplexer_1 (
    .in0({32{1'b0}}), .in1(x1_t), .in2(x2_t), .in3(x3_t), .in4(x4_t), .in5(x5_t), .in6(x6_t), .in7(x7_t),
    .in8(x8_t), .in9(x9_t), .in10(x10_t), .in11(x11_t), .in12(x12_t), .in13(x13_t), .in14(x14_t),
    .in15(x15_t), .in16(x16_t), .in17(x17_t), .in18(x18_t), .in19(x19_t), .in20(x20_t), .in21(x21_t),
    .in22(x22_t), .in23(x23_t), .in24(x24_t), .in25(x25_t), .in26(x26_t), .in27(x27_t), .in28(x28_t),
    .in29(x29_t), .in30(x30_t), .in31(x31_t), .out(rs1), .sel(rsi1));
  Multiplexer #(.select(5), .width(32)) multiplexer_2 (
    .in0({32{1'b0}}), .in1(x1_t), .in2(x2_t), .in3(x3_t), .in4(x4_t), .in5(x5_t), .in6(x6_t), .in7(x7_t),
    .in8(x8_t), .in9(x9_t), .in10(x10_t), .in11(x11_t), .in12(x12_t), .in13(x13_t), .in14(x14_t),
    .in15(x15_t), .in16(x16_t), .in17(x17_t), .in18(x18_t), .in19(x19_t), .in20(x20_t), .in21(x21_t),
    .in22(x22_t), .in23(x23_t), .in24(x24_t), .in25(x25_t), .in26(x26_t), .in27(x27_t), .in28(x28_t),
    .in29(x29_t), .in30(x30_t), .in31(x31_t), .out(rs2), .sel(rsi2));

  // Other names for the same wires on the sheet: rd_t[31:0] = rd; rdi_t[4:0] = rdi; rs1_t[31:0] = rs1;
  //   rs2_t[31:0] = rs2; rsi1_t[4:0] = rsi1; rsi2_t[4:0] = rsi2; we_t = we
endmodule

module ALU (
  input  [31:0] dataA,
  input  [31:0] dataB,
  input  [3:0] sel,
  output [31:0] dataD
);

  wire comparator_1_lt, comparator_2_lt;
  wire [31:0] addout_t, andout_t, mulout_t, orout_t, sllout_t, sltout_t, sltuout_t, sraout_t, srlout_t,
       subout_t, xorout_t;

  Adder #(.width(32)) adder_1 (.a(dataA), .b(dataB), .out(addout_t));  // open: cin, cout
  Subtractor #(.width(32)) subtractor_1 (.a(dataA), .b(dataB), .out(subout_t));  // open: bin, bout
  Shifter #(.width(32)) shifter_1 (.in(dataA), .\dist (dataB[4:0]), .out(sllout_t));
  Shifter #(.shift("lr"), .width(32)) shifter_2 (.in(dataA), .\dist (dataB[4:0]), .out(srlout_t));
  Shifter #(.shift("ar"), .width(32)) shifter_3 (.in(dataA), .\dist (dataB[4:0]), .out(sraout_t));
  assign xorout_t = dataA ^ dataB;  // XOR_Gate xor_1, 32 bits wide
  assign andout_t = dataA & dataB;  // AND_Gate and_1, 32 bits wide
  assign orout_t = dataA | dataB;  // OR_Gate or_1, 32 bits wide
  Multiplier #(.mode("twosComplement"), .width(32)) multiplier_1 (
    .a(dataA), .b(dataB), .out(mulout_t));  // open: cin, cout
  Comparator #(.width(32)) comparator_1 (.a(dataA), .b(dataB), .lt(comparator_1_lt));  // open: gt, eq
  Comparator #(.mode("unsigned"), .width(32)) comparator_2 (
    .a(dataA), .b(dataB), .lt(comparator_2_lt));  // open: gt, eq
  assign sltout_t = {{31{1'b0}}, comparator_1_lt};  // Bit_Extender bit_extender_1
  assign sltuout_t = {{31{1'b0}}, comparator_2_lt};  // Bit_Extender bit_extender_2
  Multiplexer #(.select(4), .width(32)) multiplexer_1 (
    .in0(addout_t), .in1(sllout_t), .in2(sltout_t), .in3(sltuout_t), .in4(xorout_t), .in5(srlout_t),
    .in6(orout_t), .in7(andout_t), .in8(subout_t), .in9(mulout_t), .in13(sraout_t), .in15(dataB),
    .out(dataD), .sel(sel));  // open: in10, in11, in12, in14

  // Other names for the same wires on the sheet: dataA_t[31:0] = dataA; bitstoshift_t[4:0] = dataB[4:0];
  //   dataB_t[31:0] = dataB; dataD_t[31:0] = dataD; sel_t[3:0] = sel
endmodule

module Immediate_Generator (
  input  [31:0] ins,
  input  [2:0] immsel,
  output [31:0] imm31_0
);

  wire [3:0] bspliter_1_imm1_4;
  wire [4:0] sspliter_1_imm0_4;
  wire [5:0] bspliter_1_imm5_10;
  wire [6:0] sspliter_1_imm5_11;
  wire [7:0] jspliter_1_imm12_19;
  wire [9:0] jspliter_1_imm1_10;
  wire [11:0] ispliter_1_imm;
  wire [12:11] bspliter_1_imm11;
  wire [20:11] jspliter_1_imm11;
  wire [31:0] Bimm_t, bit_extender_3_out, bit_extender_4_out, Iimm_t, jimm_t, Simm_t;
  wire [31:12] uimm_t;

  Ispliter ispliter_1 (.ins(ins), .imm(ispliter_1_imm));  // open: opcode, rd, func3, rs1
  Sspliter sspliter_1 (
    .ins(ins), .imm0_4(sspliter_1_imm0_4), .imm5_11(sspliter_1_imm5_11));  // open: opcode, func3, rs1, rs2
  BSpliter bspliter_1 (
    .ins(ins), .imm11(bspliter_1_imm11[11]), .imm1_4(bspliter_1_imm1_4), .imm5_10(bspliter_1_imm5_10),
    .imm12(bspliter_1_imm11[12]));  // open: opcode, func3, rs1, rs2
  Jspliter jspliter_1 (
    .ins(ins), .imm12_19(jspliter_1_imm12_19), .imm11(jspliter_1_imm11[11]), .imm1_10(jspliter_1_imm1_10),
    .imm20(jspliter_1_imm11[20]));  // open: opcode, rd
  Uformat uformat_1 (.ins(ins), .imm12_31(uimm_t));  // open: opcode, rd
  assign Iimm_t = {{20{ispliter_1_imm[11]}}, ispliter_1_imm};  // Bit_Extender bit_extender_1
  assign Simm_t = {{20{sspliter_1_imm5_11[6]}}, {sspliter_1_imm5_11, sspliter_1_imm0_4}};  // Bit_Extender bit_extender_2
  assign bit_extender_3_out = {{19{bspliter_1_imm11[12]}}, {bspliter_1_imm11, bspliter_1_imm5_10, bspliter_1_imm1_4, 1'b0}};  // Bit_Extender bit_extender_3
  assign bit_extender_4_out = {{11{jspliter_1_imm11[20]}}, {jspliter_1_imm11[20], jspliter_1_imm12_19, jspliter_1_imm11[11], jspliter_1_imm1_10, 1'b0}};  // Bit_Extender bit_extender_4
  Shifter #(.shift("ar"), .width(32)) shifter_1 (.in(bit_extender_3_out), .\dist (5'b00010), .out(Bimm_t));
  Shifter #(.shift("ar"), .width(32)) shifter_2 (.in(bit_extender_4_out), .\dist (5'b00010), .out(jimm_t));
  Multiplexer #(.select(3), .width(32)) multiplexer_1 (
    .in0(Iimm_t), .in1(Simm_t), .in2(Bimm_t), .in3(jimm_t), .in4({uimm_t, {12{1'b0}}}), .out(imm31_0),
    .sel(immsel));  // open: in5, in6, in7

  // Other names for the same wires on the sheet: imm_t[31:0] = imm31_0; ins_t[31:0] = ins; sel_t[2:0] = immsel
endmodule

module insmem (
  input  [15:0] address,
  input  we_imem,
  input  re_imem,
  output [4:0] rdi,
  output [4:0] rs1i,
  output [4:0] rsi2,
  output [31:0] ins
);

  wire clock_1_out;
  wire [15:0] undriven;
  wire [31:0] ram_1_dout, undriven_2;

  Clock clock_1 (.out(clock_1_out));
  RAM #(.addrWidth(16), .dataWidth(32)) ram_1 (
    .addr(undriven), .we(we_imem), .oe(re_imem), .clk(clock_1_out), .din(undriven_2), .dout(ram_1_dout));
  ROM #(.addrWidth(16), .dataWidth(32)) rom_1 (.addr(address), .data(ins));

  assign rdi = ins[11:7];
  assign rs1i = ins[19:15];
  assign rsi2 = ins[24:20];

  // Other names for the same wires on the sheet: addr[15:0] = address

  // Notes on the sheet:
  //   contents of rom_1 (hex, n*v repeats v):
  //   3e800093 113 112023 12183 abcd237 ef20213 412223 300393 710323
endmodule

module Rspliter (
  input  [31:0] ins,
  output [6:0] opcode,
  output [4:0] rd,
  output [2:0] fun3,
  output [4:0] rs1,
  output [4:0] rs2,
  output [6:0] func7
);


  assign fun3 = ins[14:12];
  assign func7 = ins[31:25];
  assign opcode = ins[6:0];
  assign rd = ins[11:7];
  assign rs1 = ins[19:15];
  assign rs2 = ins[24:20];
endmodule

module Ispliter (
  input  [31:0] ins,
  output [6:0] opcode,
  output [4:0] rd,
  output [2:0] func3,
  output [4:0] rs1,
  output [11:0] imm
);


  assign func3 = ins[14:12];
  assign imm = ins[31:20];
  assign opcode = ins[6:0];
  assign rd = ins[11:7];
  assign rs1 = ins[19:15];
endmodule

module Sspliter (
  input  [31:0] ins,
  output [6:0] opcode,
  output [4:0] imm0_4,
  output [2:0] func3,
  output [4:0] rs1,
  output [4:0] rs2,
  output [6:0] imm5_11
);


  assign func3 = ins[14:12];
  assign imm0_4 = ins[11:7];
  assign imm5_11 = ins[31:25];
  assign opcode = ins[6:0];
  assign rs1 = ins[19:15];
  assign rs2 = ins[24:20];
endmodule

module BSpliter (
  input  [31:0] ins,
  output [6:0] opcode,
  output imm11,
  output [3:0] imm1_4,
  output [2:0] func3,
  output [4:0] rs1,
  output [4:0] rs2,
  output [5:0] imm5_10,
  output imm12
);


  assign func3 = ins[14:12];
  assign imm1_4 = ins[11:8];
  assign imm5_10 = ins[30:25];
  assign imm11 = ins[7];
  assign imm12 = ins[31];
  assign opcode = ins[6:0];
  assign rs1 = ins[19:15];
  assign rs2 = ins[24:20];
endmodule

module Jspliter (
  input  [31:0] ins,
  output [6:0] opcode,
  output [4:0] rd,
  output [7:0] imm12_19,
  output imm11,
  output [9:0] imm1_10,
  output imm20
);


  assign imm1_10 = ins[30:21];
  assign imm11 = ins[20];
  assign imm12_19 = ins[19:12];
  assign imm20 = ins[31];
  assign opcode = ins[6:0];
  assign rd = ins[11:7];
endmodule

module Uformat (
  input  [31:0] ins,
  output [6:0] opcode,
  output [4:0] rd,
  output [19:0] imm12_31
);


  assign imm12_31 = ins[31:12];
  assign opcode = ins[6:0];
  assign rd = ins[11:7];
endmodule

module branch_com (
  input  [31:0] dataA,
  input  [31:0] dataB,
  input  brUn,
  output brLt,
  output brEq
);

  wire comparator_1_lt, comparator_2_lt;

  Comparator #(.width(32)) comparator_1 (.a(dataA), .b(dataB), .eq(brEq), .lt(comparator_1_lt));  // open: gt
  Comparator #(.mode("unsigned"), .width(32)) comparator_2 (
    .a(dataA), .b(dataB), .lt(comparator_2_lt));  // open: gt, eq
  Multiplexer multiplexer_1 (.in0(comparator_1_lt), .in1(comparator_2_lt), .out(brLt), .sel(brUn));

  // Other names for the same wires on the sheet: brEq_t = brEq; brLt_t = brLt; brUn_t = brUn; dataA_t[31:0] = dataA;
  //   dataB_t[31:0] = dataB
endmodule

module Control_logic (
  input  [31:0] istruction,
  input  BrLt,
  input  BrEq,
  output [3:0] ALUsle,
  output regwe,
  output [2:0] immse,
  output Bsel,
  output [2:0] Lsel,
  output Re,
  output we,
  output Asel,
  output [1:0] WBSel,
  output [1:0] Ssel,
  output brUn,
  output PCsel,
  output re_imm,
  output we_imm
);

  wire add_t, addi_t, and_2_out, and_3_out, and_4_out, and_5_out, and_6_out, and_7_out, and_45_out,
       and_46_out, and_47_out, and_48_out, and_49_out, and_50_out, and_t, andi_t, auipc_t, beq_t, Bformat,
       bge_t, bgeu_t, bltu_t, bne_t, bth_t, jal_t, jalr_t, jformat, lb_t, lbu_t, lh_t, lhu_t, lui_t, mul_t,
       not_1_out, not_2_out, not_3_out, not_4_out, not_5_out, not_6_out, or_5_out, or_6_out, or_11_out,
       or_13_out, or_14_out, or_16_out, or_17_out, or_18_out, or_19_out, or_20_out, or_21_out, or_22_out,
       or_33_out, or_t, ori_t, sb_t, Sformat, sll_t, slli_t, slt_t, slti_t, sltiu_t, sltu_t, sra_t, srai_t,
       srl_t, srli_t, sub_t, xor_t, xori_t;

  or or_1 (jformat, jalr_t, jal_t);
  and and_1 (mul_t, ~istruction[2], ~istruction[3], istruction[4], istruction[5], ~istruction[6], ~istruction[12], ~istruction[13], ~istruction[14], istruction[25]);  // AND_Gate
  not not_1 (not_1_out, BrEq);
  not not_2 (not_2_out, BrLt);
  not not_3 (not_3_out, BrLt);
  and and_2 (and_2_out, bltu_t, BrLt);
  and and_3 (and_3_out, BrLt, bth_t);
  and and_4 (and_4_out, beq_t, BrEq);
  and and_5 (and_5_out, bne_t, not_1_out);
  and and_6 (and_6_out, bge_t, not_2_out);
  and and_7 (and_7_out, bgeu_t, not_3_out);
  and and_8 (jalr_t, istruction[2], ~istruction[3], ~istruction[4], istruction[5], istruction[6]);  // AND_Gate
  and and_9 (beq_t, ~istruction[2], ~istruction[3], ~istruction[4], istruction[5], istruction[6], ~istruction[12], ~istruction[13], ~istruction[14]);  // AND_Gate
  and and_10 (bne_t, ~istruction[2], ~istruction[3], ~istruction[4], istruction[5], istruction[6], istruction[12], ~istruction[13], ~istruction[14]);  // AND_Gate
  and and_11 (bge_t, ~istruction[2], ~istruction[3], ~istruction[4], istruction[5], istruction[6], istruction[12], ~istruction[13], istruction[14]);  // AND_Gate
  or or_2 (PCsel, and_2_out, and_3_out, and_4_out, jformat, and_5_out, and_6_out, and_7_out);
  and and_12 (bgeu_t, ~istruction[2], ~istruction[3], ~istruction[4], istruction[5], istruction[6], istruction[12], istruction[13], istruction[14]);  // AND_Gate
  and and_13 (add_t, ~istruction[2], ~istruction[3], istruction[4], istruction[5], ~istruction[6], ~istruction[12], ~istruction[13], ~istruction[14], ~istruction[30]);  // AND_Gate
  and and_14 (sub_t, ~istruction[2], ~istruction[3], istruction[4], istruction[5], ~istruction[6], ~istruction[12], ~istruction[13], ~istruction[14], istruction[30]);  // AND_Gate
  and and_15 (or_t, ~istruction[2], ~istruction[3], istruction[4], istruction[5], ~istruction[6], ~istruction[12], istruction[13], istruction[14], ~istruction[30]);  // AND_Gate
  and and_16 (and_t, ~istruction[2], ~istruction[3], istruction[4], istruction[5], ~istruction[6], istruction[12], istruction[13], istruction[14], ~istruction[30]);  // AND_Gate
  and and_17 (sll_t, ~istruction[2], ~istruction[3], istruction[4], istruction[5], ~istruction[6], istruction[12], ~istruction[13], ~istruction[14], istruction[30]);  // AND_Gate
  and and_18 (sltu_t, ~istruction[2], ~istruction[3], istruction[4], istruction[5], ~istruction[6], istruction[12], istruction[13], ~istruction[14], istruction[30]);  // AND_Gate
  and and_19 (slli_t, ~istruction[2], ~istruction[3], istruction[4], ~istruction[5], ~istruction[6], istruction[12], ~istruction[13], ~istruction[14], ~istruction[30]);  // AND_Gate
  and and_20 (srli_t, ~istruction[2], ~istruction[3], istruction[4], ~istruction[5], ~istruction[6], istruction[12], ~istruction[13], istruction[14], ~istruction[30]);  // AND_Gate
  and and_21 (addi_t, ~istruction[2], ~istruction[3], istruction[4], ~istruction[5], ~istruction[6], ~istruction[12], ~istruction[13], ~istruction[14]);  // AND_Gate
  and and_22 (sltiu_t, ~istruction[2], ~istruction[3], istruction[4], ~istruction[5], ~istruction[6], istruction[12], istruction[13], ~istruction[14]);  // AND_Gate
  and and_23 (andi_t, ~istruction[2], ~istruction[3], istruction[4], ~istruction[5], ~istruction[6], istruction[12], istruction[13], istruction[14]);  // AND_Gate
  and and_24 (bth_t, ~istruction[2], ~istruction[3], ~istruction[4], istruction[5], istruction[6], ~istruction[12], ~istruction[13], istruction[14]);  // AND_Gate
  and and_25 (bltu_t, ~istruction[2], ~istruction[3], ~istruction[4], istruction[5], istruction[6], ~istruction[12], istruction[13], istruction[14]);  // AND_Gate
  or or_3 (brUn, bltu_t, bgeu_t);
  and and_26 (srl_t, ~istruction[2], ~istruction[3], istruction[4], istruction[5], ~istruction[6], istruction[12], ~istruction[13], istruction[14], ~istruction[30]);  // AND_Gate
  and and_27 (xor_t, ~istruction[2], ~istruction[3], istruction[4], istruction[5], ~istruction[6], ~istruction[12], ~istruction[13], istruction[14], ~istruction[30]);  // AND_Gate
  and and_28 (xori_t, ~istruction[2], ~istruction[3], istruction[4], ~istruction[5], ~istruction[6], ~istruction[12], ~istruction[13], istruction[14]);  // AND_Gate
  or or_4 (Bformat, bltu_t, bgeu_t, bge_t, bne_t, beq_t, bth_t);
  or or_5 (or_5_out, or_t, sra_t, xor_t, srl_t, and_t);
  or or_6 (or_6_out, ori_t, srai_t, xori_t, srli_t, andi_t);
  and and_29 (slt_t, ~istruction[2], ~istruction[3], istruction[4], istruction[5], ~istruction[6], ~istruction[12], istruction[13], ~istruction[14], ~istruction[30]);  // AND_Gate
  and and_30 (slti_t, ~istruction[2], ~istruction[3], istruction[4], ~istruction[5], ~istruction[6], ~istruction[12], istruction[13], ~istruction[14]);  // AND_Gate
  and and_31 (Ssel[1], ~istruction[2], ~istruction[3], ~istruction[4], istruction[5], ~istruction[6], ~istruction[12], istruction[13]);  // AND_Gate
  and and_32 (srai_t, ~istruction[2], ~istruction[3], istruction[4], ~istruction[5], ~istruction[6], istruction[12], ~istruction[13], istruction[14], istruction[30]);  // AND_Gate
  and and_33 (ori_t, ~istruction[2], ~istruction[3], istruction[4], ~istruction[5], ~istruction[6], ~istruction[12], istruction[13], istruction[14]);  // AND_Gate
  and and_34 (sb_t, ~istruction[2], ~istruction[3], ~istruction[4], istruction[5], ~istruction[6], ~istruction[12], ~istruction[13]);  // AND_Gate
  and and_35 (Ssel[0], ~istruction[2], ~istruction[3], ~istruction[4], istruction[5], ~istruction[6], istruction[12], ~istruction[13]);  // AND_Gate
  or or_7 (ALUsle[2], or_5_out, lui_t, or_6_out);
  or or_8 (ALUsle[3], sub_t, srai_t, mul_t, sra_t, lui_t);
  or or_9 (ALUsle[1], slti_t, sltiu_t, slt_t, or_t, lui_t, and_t, sltu_t, andi_t, ori_t);
  or or_10 (we, sb_t, Ssel[0], Ssel[1]);
  and and_36 (sra_t, ~istruction[2], ~istruction[3], istruction[4], istruction[5], ~istruction[6], istruction[12], ~istruction[13], istruction[14], istruction[30]);  // AND_Gate
  or or_11 (or_11_out, Lsel[1], lb_t, lh_t, lhu_t, lbu_t);
  and and_37 (lb_t, ~istruction[2], ~istruction[3], ~istruction[4], ~istruction[5], ~istruction[6], ~istruction[12], ~istruction[13], ~istruction[14]);  // AND_Gate
  and and_38 (lh_t, ~istruction[2], ~istruction[3], ~istruction[4], ~istruction[5], ~istruction[6], istruction[12], ~istruction[13], ~istruction[14]);  // AND_Gate
  or or_12 (Re, or_11_out, we);
  and and_39 (jal_t, istruction[2], istruction[3], ~istruction[4], istruction[5], istruction[6]);  // AND_Gate
  and and_40 (auipc_t, istruction[2], ~istruction[3], istruction[4], ~istruction[5], ~istruction[6]);  // AND_Gate
  and and_41 (lui_t, istruction[2], ~istruction[3], istruction[4], istruction[5], ~istruction[6]);  // AND_Gate
  or or_13 (or_13_out, Lsel[1], lb_t, lh_t, lhu_t, lbu_t);
  or or_14 (or_14_out, Lsel[1], lb_t, lh_t, lhu_t, lbu_t);
  or or_15 (Sformat, sb_t, Ssel[0], Ssel[1]);
  or or_16 (or_16_out, add_t, sub_t, or_t, and_t, srl_t, sll_t, xor_t, sra_t, slt_t, sltu_t);
  or or_17 (or_17_out, addi_t, sltiu_t, slli_t, srli_t, srai_t, xori_t, slti_t, andi_t, ori_t);
  or or_18 (or_18_out, addi_t, sltiu_t, slli_t, srli_t, srai_t, xori_t, slti_t, andi_t, ori_t, jalr_t);
  or or_19 (or_19_out, add_t, sub_t, or_t, and_t, srl_t, sll_t, xor_t, sra_t, slt_t, sltu_t);
  or or_20 (or_20_out, addi_t, sltiu_t, slli_t, srli_t, srai_t, xori_t, slti_t, andi_t, ori_t, jalr_t);
  or or_21 (or_21_out, immse[2], jal_t, mul_t);
  and and_42 (Lsel[1], ~istruction[2], ~istruction[3], ~istruction[4], ~istruction[5], ~istruction[6], ~istruction[12], istruction[13], ~istruction[14]);  // AND_Gate
  and and_43 (lhu_t, ~istruction[2], ~istruction[3], ~istruction[4], ~istruction[5], ~istruction[6], istruction[12], ~istruction[13], istruction[14]);  // AND_Gate
  or or_22 (or_22_out, jalr_t, jal_t);
  or or_23 (WBSel[0], or_16_out, or_17_out, immse[2]);
  or or_24 (regwe, or_19_out, or_13_out, or_20_out, or_21_out);
  and and_44 (lbu_t, ~istruction[2], ~istruction[3], ~istruction[4], ~istruction[5], ~istruction[6], ~istruction[12], ~istruction[13], istruction[14]);  // AND_Gate
  or or_25 (Bsel, immse[2], or_18_out, or_14_out, Sformat, Asel, or_22_out);
  or or_26 (Lsel[0], lh_t, lhu_t);
  or or_27 (WBSel[1], jalr_t, jal_t);
  or or_28 (Lsel[2], lhu_t, lbu_t);
  or or_29 (immse[2], auipc_t, lui_t);
  or or_30 (ALUsle[0], lui_t, srai_t, sltiu_t, slli_t, sra_t, sltu_t, and_t, srl_t, srli_t, andi_t, sll_t, mul_t);
  or or_31 (immse[0], Sformat, jal_t);
  or or_32 (immse[1], Bformat, jal_t);
  and and_45 (and_45_out, bltu_t, BrLt);
  and and_46 (and_46_out, BrLt, bth_t);
  and and_47 (and_47_out, beq_t, BrEq);
  and and_48 (and_48_out, bne_t, not_4_out);
  not not_4 (not_4_out, BrEq);
  not not_5 (not_5_out, BrLt);
  not not_6 (not_6_out, BrLt);
  and and_49 (and_49_out, bge_t, not_5_out);
  and and_50 (and_50_out, bgeu_t, not_6_out);
  or or_33 (or_33_out, and_45_out, and_46_out, and_47_out, and_48_out, and_49_out, and_50_out, auipc_t);
  or or_34 (Asel, or_33_out, jal_t);

  assign re_imm = 1'b1;
  assign we_imm = 1'b0;

  // Other names for the same wires on the sheet: as0_t = ALUsle[0]; as1_t = ALUsle[1]; as2_t = ALUsle[2];
  //   as3_t = ALUsle[3]; Asel_t = Asel; breq_t = BrEq; brlt_t = BrLt; a0_t = immse[0]; a1_t = immse[1];
  //   a2_t = immse[2]; Uformat = immse[2]; i2_t = istruction[2]; i3_t = istruction[3]; i4 = istruction[4];
  //   i5 = istruction[5]; i6 = istruction[6]; i12 = istruction[12]; i13 = istruction[13]; i14 = istruction[14];
  //   i25 = istruction[25]; i30 = istruction[30]; lw_t = Lsel[1]; sh_t = Ssel[0]; sw_t = Ssel[1]
endmodule

module Loadcircuit (
  input  [31:0] Adress,
  input  [31:0] D,
  input  [2:0] lSel,
  output [31:0] Loaded
);

  wire bitselector_2_out;
  wire [1:0] bitselector_1_out;
  wire [7:0] bitselector_4_out;
  wire [15:0] bitselector_3_out;
  wire [31:0] lb_t, lbu_t, lh_t, lhu_t;

  BitSelector #(.group(2), .width(32)) bitselector_1 (.in(Adress), .out(bitselector_1_out), .sel(4'b0000));
  BitSelector #(.width(32)) bitselector_2 (.in(Adress), .out(bitselector_2_out), .sel({5{1'b0}}));
  BitSelector #(.group(16), .width(32)) bitselector_3 (.in(D), .out(bitselector_3_out), .sel(bitselector_2_out));
  BitSelector #(.group(8), .width(32)) bitselector_4 (.in(D), .out(bitselector_4_out), .sel(bitselector_1_out));
  assign lh_t = {{16{bitselector_3_out[15]}}, bitselector_3_out};  // Bit_Extender bit_extender_1
  assign lhu_t = {{16{1'b0}}, bitselector_3_out};  // Bit_Extender bit_extender_2
  assign lb_t = {{24{bitselector_4_out[7]}}, bitselector_4_out};  // Bit_Extender bit_extender_3
  assign lbu_t = {{24{1'b0}}, bitselector_4_out};  // Bit_Extender bit_extender_4
  Multiplexer #(.select(3), .width(32)) multiplexer_1 (
    .in0(lb_t), .in1(lh_t), .in2(D), .in4(lbu_t), .in5(lhu_t), .out(Loaded), .sel(lSel));  // open: in3, in6, in7

  // Other names for the same wires on the sheet: A_t[31:0] = Adress; lw_t[31:0] = D
endmodule

module Storecircuit (
  input  [31:0] Data,
  input  [1:0] Ssel,
  input  [31:0] address,
  input  [31:0] load,
  output [31:0] Store
);

  wire [1:0] bitselector_2_out;
  wire [4:0] Shift_t;
  wire [4:4] s_t, Sl_t;
  wire [15:0] bitselector_3_out;
  wire [31:0] and_1_out, bit_extender_1_out, bit_extender_2_out, not_2_out, sb_t, sh_t, shifter_1_out,
       shifter_2_out, shifter_3_out, shifter_4_out, shifter_5_out;

  BitSelector #(.width(32)) bitselector_1 (.in(address), .out(s_t[4]), .sel(5'b00001));
  not not_1 (Sl_t[4], s_t[4]);
  BitSelector #(.group(2), .width(32)) bitselector_2 (.in(address), .out(bitselector_2_out), .sel(4'b0000));
  BitSelector #(.group(16), .width(32)) bitselector_3 (.in(load), .out(bitselector_3_out), .sel(s_t[4]));
  assign bit_extender_1_out = {{30{bitselector_2_out[1]}}, bitselector_2_out};  // Bit_Extender bit_extender_1
  assign bit_extender_2_out = {{16{1'b0}}, bitselector_3_out};  // Bit_Extender bit_extender_2
  Shifter #(.width(32)) shifter_1 (.in(bit_extender_1_out), .\dist (5'b00011), .out(shifter_1_out));
  Shifter #(.width(32)) shifter_2 (.in(bit_extender_2_out), .\dist ({s_t[4], 4'b0000}), .out(shifter_2_out));
  Shifter #(.width(32)) shifter_3 (.in(Data), .\dist ({Sl_t[4], 4'b0000}), .out(shifter_3_out));
  BitSelector #(.group(5), .width(32)) bitselector_4 (.in(shifter_1_out), .out(Shift_t), .sel(3'b000));
  assign sh_t = shifter_2_out | shifter_3_out;  // OR_Gate or_1, 32 bits wide
  Shifter #(.width(32)) shifter_4 (.in(32'hff), .\dist (Shift_t), .out(shifter_4_out));
  assign not_2_out = ~shifter_4_out;  // NOT_Gate not_2, 32 bits wide
  Multiplexer #(.select(2), .width(32)) multiplexer_1 (
    .in0(sb_t), .in1(sh_t), .in2(Data), .out(Store), .sel(Ssel));  // open: in3
  assign and_1_out = not_2_out & load;  // AND_Gate and_1, 32 bits wide
  Shifter #(.width(32)) shifter_5 (.in(Data), .\dist (Shift_t), .out(shifter_5_out));
  assign sb_t = shifter_5_out | and_1_out;  // OR_Gate or_2, 32 bits wide

  // Other names for the same wires on the sheet: A_t[31:0] = address; D_T[31:0] = Data; L_t[31:0] = load;
  //   Ssel_t[1:0] = Ssel
endmodule
